# Fritzing sketch FE_M5Stack_Main_PCB (saved by Fritzing 0.9.3b)
circuit board: 8cm x 5cm
breadboards: 1

parts:
  MP1584EN_Board1 = MP1584EN Power Regulator Board [part_number=MP1584EN]
  Stack = female pin header, 15 pins [form="♀ (female)"]
  M5 = female pin header, 15 pins [form="♀ (female)"]
  Encoders = female pin header, 3 pins [form="♀ (female)"]
  J13 = female pin header, 3 pins [form="♀ (female)"]
  Servos = female pin header, 2 pins [form="♀ (female)"]
  J14 = female pin header, 2 pins [form="♀ (female)"]
  J15 = female pin header, 2 pins [form="♀ (female)"]
  VBAT = female pin header, 2 pins [form="♀ (female)"]
  MOUT = female pin header, 2 pins [form="♀ (female)"]
  ES = female pin header, 1 pin [form="♀ (female)"]
  C = female pin header, 6 pins [form="♀ (female)"]
  J16 = female pin header, 3 pins [form="♀ (female)"]
  LLC1 = Logic Level Converter [package="Breakout board"]
  I2C_5V = female pin header, 4 pins [form="♀ (female)"]
  I2C_3V3 = female pin header, 4 pins [form="♀ (female)"]
  J17 = female pin header, 4 pins [form="♀ (female)"]
  J18 = female pin header, 4 pins [form="♀ (female)"]
  MPU6050 = InvenSense MPU6050
  R1 = Resistor [tolerance=±5% resistance=10k package=THT]
  R2 = Resistor [tolerance=±5% resistance=10k package=THT]
  R3 = Resistor [tolerance=±5% resistance=10k package=THT]
  VBAT_M5 = female pin header, 2 pins [form="♀ (female)"]
  J11 = female pin header, 3 pins [form="♀ (female)"]
  J10 = female pin header, 3 pins [form="♀ (female)"]
  J19 = female pin header, 1 pin [form="♀ (female)"]

nets:
  N1: MP1584EN_Board1.IN_-, MP1584EN_Board1.OUT_-, M5.pin13, M5.pin14, M5.pin15, J15.pin1, J15.pin2, VBAT.pin2, C.pin1, J16.pin1, J16.pin2, J16.pin3, LLC1.H-GND, I2C_5V.pin4, I2C_3V3.pin4, J17.pin4, J18.pin4, VBAT_M5.pin1
  N2: MP1584EN_Board1.IN_+, C.pin4, J11.pin1
  N3: MP1584EN_Board1.OUT_+, J13.pin1, J13.pin2, J13.pin3, J14.pin1, J14.pin2, LLC1.HV, I2C_5V.pin3, J17.pin3
  N4: Stack.pin1, VBAT_M5.pin2
  N5: Stack.pin3, Encoders.pin3, R1.Pin_0
  N6: Stack.pin5, MPU6050.INT
  N7: Stack.pin6, J19.pin1
  N8: Stack.pin7, LLC1.LV2, I2C_3V3.pin2, J18.pin2, MPU6050.SCL
  N9: Stack.pin8, Servos.pin2
  N10: Stack.pin10, LLC1.LV, I2C_3V3.pin3, J18.pin3, MPU6050.VCC, R1.Pin_1, R2.Pin_1, R3.Pin_1
  N11: Stack.pin11, Servos.pin1
  N12: Stack.pin14, Encoders.pin1, R3.Pin_0
  N13: Stack.pin15, Encoders.pin2, R2.Pin_0
  N14: M5.pin7, LLC1.LV1, I2C_3V3.pin1, J18.pin1, MPU6050.SDA
  N15: M5.pin8, ES.pin1
  N16: VBAT.pin1, J11.pin3, J10.pin2
  N17: MOUT.pin1, C.pin3
  N18: MOUT.pin2, C.pin2
  N19: C.pin5, C.pin6
  N20: LLC1.L-GND, MPU6050.GND
  N21: LLC1.HV2, I2C_5V.pin2, J17.pin2
  N22: LLC1.HV1, I2C_5V.pin1, J17.pin1

notes:
  Pinout ESC (Izq a der):
  PWM, Interruptor, Interruptor (hay que unirlos), VM, Out1, Out2, GND
  Asignacion pines:
  ESC - G16 (RX2)
  Servos - G17 (TX2), G26 (DAC)
  Enc (Ext PullUp)- G34 (I2S_IN), G35 (ADC), G36 (ADC)
  MPU (INT) - G13 (I2S_WS)
  I2C - G21 (SDA), G22 (SCL)

custom parts:
  MP1584EN Power Regulator Board: The MP1584EN is a high frequency step-down switching regulator. The input voltage range is 4.5V to 28V. The output voltage is set by the board's potentiometer.
  Logic Level Converter: 5V to/from 3.3V logic level converter
